// Logisim project 8-bit-cpu.circ as structural Verilog: 4 circuits, main circuit main
// IR0
module main (
  input  in_1,
  input  Reset,
  input  [1:0] in_3,
  output [7:0] out_4
);

  wire and_1_out, and_2_out, and_3_out, and_4_out, and_5_out, and_6_out, branch_logic_1_branch_output,
       clock_1_out, comparator_1_eq, comparator_2_eq, decoder_1_out0, decoder_1_out1, decoder_1_out2,
       decoder_1_out3, decoder_1_out7, decoder_2_out0, decoder_2_out1, decoder_2_out2, decoder_2_out3,
       decoder_2_out4, decoder_2_out5, decoder_2_out6, decoder_2_out7, multiplexer_1_out, not_1_out,
       or_1_out, or_2_out, or_4_out, or_5_out, Step_out;
  wire [2:0] IR0_q;
  wire [3:0] alu_1_status_output, counter_1_q;
  wire [7:0] alu_1_data_output, controlled_buffer_6_out, controlled_buffer_18_out, IR1_q, IR2_q, IR3_q,
       LRHI_q, LRLO_q, register_3_q, rom_1_data;
  wire [7:3] IR0_q_2;
  wire [15:0] controlled_buffer_1_out, PC_q, register_2_q;

  or or_1 (or_1_out, Reset, 1'b0);
  Button Halt ();  // open: out
  assign controlled_buffer_1_out = or_5_out ? PC_q : 16'bz;  // Controlled_Buffer controlled_buffer_1
  Counter #(.width(16), .max('hffff)) PC (
    .load(or_1_out), .D(controlled_buffer_1_out), .count(or_5_out), .Q(PC_q), .clk(multiplexer_1_out));  // open: carry, clr
  assign controlled_buffer_1_out = Reset ? 16'h100 : 16'bz;  // Controlled_Buffer controlled_buffer_2
  Controlled_Buffer #(.width(8)) controlled_buffer_3 (.en(1'b0));  // open: in, out
  assign controlled_buffer_1_out = 1'b0 ? {{8{1'b1}}, controlled_buffer_6_out} : 16'bz;  // Controlled_Buffer controlled_buffer_4
  assign controlled_buffer_1_out = branch_logic_1_branch_output ? register_2_q : 16'bz;  // Controlled_Buffer controlled_buffer_5
  branch_logic branch_logic_1 (
    .Operation_Select(IR0_q), .Status_input(alu_1_status_output), .Branch_output(branch_logic_1_branch_output));  // open: Branch_enable
  assign controlled_buffer_6_out = and_1_out ? IR1_q : 8'bz;  // Controlled_Buffer controlled_buffer_6
  assign controlled_buffer_6_out = and_3_out ? IR2_q : 8'bz;  // Controlled_Buffer controlled_buffer_7
  Controlled_Buffer #(.width(8)) controlled_buffer_8 (.in(IR3_q), .out(controlled_buffer_6_out));  // open: en
  Register LRLO (.D(controlled_buffer_1_out[7:0]), .Q(LRLO_q), .clk(multiplexer_1_out));  // open: en, clr
  Register LRHI (.D(controlled_buffer_1_out[15:8]), .Q(LRHI_q), .clk(multiplexer_1_out));  // open: en, clr
  Comparator #(.width(2)) comparator_1 (
    .a(controlled_buffer_1_out[15:14]), .b(2'b11), .eq(comparator_1_eq));  // open: gt, lt
  Comparator comparator_2 (.a(controlled_buffer_1_out[15:8]), .b(8'h1), .eq(comparator_2_eq));  // open: gt, lt
  Register register_1 (.D(out_4), .Q(register_2_q[15:8]), .clk(multiplexer_1_out));  // open: en, clr
  Register register_2 (.D(out_4), .Q(register_2_q[7:0]), .clk(multiplexer_1_out));  // open: en, clr
  ALU alu_1 (
    .Operation_Select(IR0_q), .A(register_2_q[15:8]), .B(register_2_q[7:0]), .Data_output(alu_1_data_output),
    .Status_output(alu_1_status_output));
  Register IR0 (.D(out_4), .en(decoder_2_out0), .Q({IR0_q_2, IR0_q}), .clk(multiplexer_1_out));  // open: clr
  Register IR1 (.D(out_4), .en(decoder_2_out1), .Q(IR1_q), .clk(multiplexer_1_out));  // open: clr
  Register IR2 (.D(out_4), .en(decoder_2_out2), .Q(IR2_q), .clk(multiplexer_1_out));  // open: clr
  Register IR3 (.D(out_4), .en(decoder_2_out3), .Q(IR3_q), .clk(multiplexer_1_out));  // open: clr
  assign out_4 = 1'b0 ? LRLO_q : 8'bz;  // Controlled_Buffer controlled_buffer_9
  assign out_4 = 1'b0 ? LRHI_q : 8'bz;  // Controlled_Buffer controlled_buffer_10
  assign out_4 = 1'b0 ? register_2_q[15:8] : 8'bz;  // Controlled_Buffer controlled_buffer_11
  assign out_4 = 1'b0 ? register_2_q[7:0] : 8'bz;  // Controlled_Buffer controlled_buffer_12
  assign out_4 = 1'b0 ? alu_1_data_output : 8'bz;  // Controlled_Buffer controlled_buffer_13
  and and_1 (and_1_out, and_6_out, ~IR0_q_2[6]);  // AND_Gate
  assign out_4 = and_2_out ? IR1_q : 8'bz;  // Controlled_Buffer controlled_buffer_14
  and and_2 (and_2_out, and_6_out, IR0_q_2[6]);
  assign out_4 = and_4_out ? IR2_q : 8'bz;  // Controlled_Buffer controlled_buffer_15
  and and_3 (and_3_out, decoder_2_out5, ~IR0_q_2[7]);  // AND_Gate
  and and_4 (and_4_out, decoder_2_out5, IR0_q_2[7]);
  RAM #(.addrWidth(14)) ram_1 (
    .addr(controlled_buffer_1_out[13:0]), .data(out_4), .sel(comparator_1_eq));  // open: clk, ld, clr
  assign out_4 = comparator_2_eq ? rom_1_data : 8'bz;  // Controlled_Buffer controlled_buffer_16
  ROM rom_1 (.addr(controlled_buffer_1_out[7:0]), .data(rom_1_data), .sel(comparator_2_eq));
  Register register_3 (.D(out_4), .en(or_2_out), .Q(register_3_q), .clk(multiplexer_1_out));  // open: clr
  or or_2 (or_2_out, and_5_out, decoder_2_out6);
  and and_5 (and_5_out, decoder_1_out7, decoder_2_out4);
  and and_6 (and_6_out, decoder_2_out4, ~decoder_1_out7);  // AND_Gate
  assign out_4 = 1'b0 ? register_3_q : 8'bz;  // Controlled_Buffer controlled_buffer_17
  Clock clock_1 (.out(clock_1_out));
  Button Step (.out(Step_out));
  Multiplexer #(.enable("false")) multiplexer_1 (
    .in0(clock_1_out), .in1(Step_out), .out(multiplexer_1_out), .sel(in_1));
  // OR_Gate or_3 is placed but not wired
  Hex_Digit_Display hex_digit_display_1 (.value(out_4[7:4]));  // open: dp
  Hex_Digit_Display hex_digit_display_2 (.value(out_4[3:0]));  // open: dp
  Controlled_Buffer #(.width(8)) controlled_buffer_18 (.out(controlled_buffer_18_out), .en(1'b1));  // open: in
  not not_1 (not_1_out, or_4_out);
  Decoder #(.select(3), .enable("false")) decoder_1 (
    .out0(decoder_1_out0), .out1(decoder_1_out1), .out2(decoder_1_out2), .out3(decoder_1_out3),
    .out7(decoder_1_out7), .sel(IR0_q_2[5:3]));  // open: out4, out5, out6
  // AND_Gate and_7 is placed but not wired
  TTY tty_1 ();  // open: data, clk, we, clr
  Keyboard keyboard_1 ();  // open: clk, re, clr, avail, data
  or or_4 (or_4_out, Reset, decoder_2_out7);
  Counter #(.width(4), .max('hf)) counter_1 (
    .load(or_4_out), .D(4'b0000), .count(not_1_out), .Q(counter_1_q), .clk(multiplexer_1_out));  // open: carry, clr
  or or_5 (or_5_out, decoder_2_out0, decoder_2_out1, decoder_2_out2, decoder_2_out3);
  // OR_Gate or_6 is placed but not wired
  Decoder #(.select(3), .enable("false")) decoder_2 (
    .out0(decoder_2_out0), .out1(decoder_2_out1), .out2(decoder_2_out2), .out3(decoder_2_out3),
    .out4(decoder_2_out4), .out5(decoder_2_out5), .out6(decoder_2_out6), .out7(decoder_2_out7),
    .sel(counter_1_q[2:0]));

  // Notes on the sheet:
  //   contents of rom_1 (hex, n*v repeats v):
  //   1 2 3 4 5 6 7 8 9 10 11 12 13 14 15 16
endmodule

module branch_logic (
  input  Branch_enable,
  input  [2:0] Operation_Select,
  input  [3:0] Status_input,
  output Branch_output
);


  assign Branch_output = 1'b0;
endmodule

module ALU (
  input  [2:0] Operation_Select,
  input  [7:0] A,
  input  [7:0] B,
  output [7:0] Data_output,
  output [3:0] Status_output
);


  assign Data_output = A;
  assign Status_output = 4'b1111;
endmodule

module Control_logic (
  input  Clock_in,
  input  Step,
  input  Halted,
  input  [3:0] State_counter,
  input  [2:0] Opcode,
  input  Mode_A,
  input  Mode_B,
  input  Reset,
  input  Interrupt,
  output memory_read,
  output PC_read,
  output A_read,
  output B_read,
  output IR2imm,
  output IR2_zp,
  output Clock_Out,
  output IR3_imm,
  output IR3_zp,
  output IR4_zp,
  output Acc_read,
  output ALU_read,
  output Branch_enable,
  output Hi,
  output Lo,
  output Reset_read,
  output Interrupt_read,
  output Reset_state_counter,
  output PC_write,
  output PC_inc,
  output memory_write,
  output A_write,
  output B_write,
  output Acc_write,
  output IR1_Write,
  output IR2_Write,
  output IR3_Write,
  output IR4_Write,
  output A_write_2,
  output A_write_3
);

  wire and_2_out, and_5_out, and_6_out, and_7_out, decoder_1_out2, decoder_1_out3, decoder_1_out4,
       decoder_2_out6, or_5_out, or_7_out;

  // OR_Gate or_1 is placed but not wired
  // AND_Gate and_1 is placed but not wired
  Decoder #(.select(3), .enable("false")) decoder_1 (
    .out2(decoder_1_out2), .out3(decoder_1_out3), .out4(decoder_1_out4), .sel(Opcode));  // open: out0, out1, out5, out6, out7
  // AND_Gate and_2 has open pins: out=and_2_out
  Multiplexer #(.enable("false")) multiplexer_1 (.in0(Clock_in), .in1(Step), .out(Clock_Out), .sel(Halted));
  // OR_Gate or_2 has open pins: in1=and_2_out, out=open
  Decoder #(.select(3), .enable("false")) decoder_2 (
    .out0(IR1_Write), .out1(IR2_Write), .out2(IR3_Write), .out3(IR4_Write), .out4(A_write), .out5(B_write),
    .out6(decoder_2_out6), .out7(Reset_state_counter), .sel(State_counter[2:0]));
  or or_3 (PC_inc, IR1_Write, IR2_Write, IR3_Write, IR4_Write);
  or or_4 (Acc_write, A_write, decoder_2_out6);
  and and_3 (IR2_zp, Mode_A, A_write);
  and and_4 (IR3_zp, Mode_B, B_write);
  or or_5 (or_5_out, decoder_1_out2, decoder_1_out3);
  or or_6 (memory_read, IR2_zp, IR3_zp, PC_inc, and_5_out);
  and and_5 (and_5_out, decoder_2_out6, or_5_out);
  or or_7 (or_7_out, A_write, decoder_2_out6);
  and and_6 (and_6_out, or_7_out, decoder_1_out4);
  and and_7 (and_7_out, decoder_1_out4, B_write);
  and and_8 (Hi, decoder_1_out4, A_write);
  and and_9 (Lo, decoder_1_out4, decoder_2_out6);
  or or_8 (PC_read, PC_inc, and_6_out);
endmodule
